# Fritzing sketch Сircuit (saved by Fritzing 0.9.4)
breadboards: 1

parts:
  Компонент1 = Arduino Uno (Rev3)
  U1 = ESP8266 NodeMCU LoLin module
  M1 = gy-213V
  KY-1 = Keyes Relay [package=THT]  # not connected
  KY-2 = Keyes Relay [package=THT]  # not connected
  S2 = Momentary Switch [package=ksa_sealed_tac_switch]  # not connected

nets:
  N1: Компонент1.A4/SDA, U1.D1, M1.SDA
  N2: Компонент1.A5/SCL, U1.D2, M1.SCL
  N3: Компонент1.D5_PWM, U1.TX
  N4: Компонент1.D6_PWM, U1.RX
  3V3: Компонент1.3V3, M1.VIN
  GND: Компонент1.GND, U1.GND, M1.GND

custom parts:
  ESP8266 NodeMCU LoLin module: ESP8266 based NodeMCU
  gy-213V: GY-213V-HDC1080 Low Power High Precision Humidity Temperature Sensor Module.
  Keyes Relay: The Keyes 5V relay module is suitable for SCM development, home appliance control. It uses a 5V~12V TIL control signal which can control DC / AC signal.
